# Fritzing sketch indoor_air_quality (saved by Fritzing 0.7.0b)
breadboards: 1

parts:
  U1 = Spark Core (v1.0)
  Figaro_TGS_2602_Gas_Sensor1 = Figaro TGS 2602 Gas Sensor
  J1 = female pin header, 4 pins [form="♀ (female)"]
  WSP-2110_HCHO_Gas_Sensor1 = WSP-2110  # not connected
  LED1 = RGB LED (com. cathode, rbg) [package="5 mm [THT]"]
  R1 = Resistor [tolerance=±5% resistance=1k package=THT]
  R2 = Resistor [tolerance=±5% resistance=4.7k package=THT]
  R3 = Resistor [tolerance=±5% resistance=10k package=THT]
  R4 = Resistor [tolerance=±5% resistance=1k package=THT]
  R5 = Resistor [tolerance=±5% resistance=1k package=THT]
  R6 = Resistor [tolerance=±5% resistance=1k package=THT]
  J2 = female pin header, 4 pins [form="♀ (female)"]
  Part1 = USB Type A Female Breakout Board [part_number=BOB-12700]  # not connected
  C1 = Electrolytic Capacitor [capacitance=1000µF package="300 mil [THT, electrolytic]"]

nets:
  N1: U1.A0, Figaro_TGS_2602_Gas_Sensor1.pin_2, R1.Pin_0
  N2: U1.A2, U1.3V3
  N3: U1.A3, U1.A6, R2.Pin_0, R5.Pin_0
  N4: U1.A5, U1.VIN, Figaro_TGS_2602_Gas_Sensor1.pin_3, Figaro_TGS_2602_Gas_Sensor1.pin_4, R4.Pin_0
  N5: U1.A7, R6.Pin_0
  N6: U1.GND, Figaro_TGS_2602_Gas_Sensor1.pin_1, R1.Pin_1, R2.Pin_1
  N7: U1.D1, J1.pin4
  N8: U1.D2, R3.Pin_0, J2.pin2
  N9: J1.pin1, LED1.blue_anode, J2.pin4, C1.-
  N10: J1.pin2, C1.+
  N11: LED1.red_anode, R6.Pin_1
  N12: LED1.common_cathode, R5.Pin_1
  N13: LED1.green_anode, R4.Pin_1
  N14: R3.Pin_1, J2.pin1

notes:
  Grove
  Dust
  Sensor
  DHT22
  16V 2200 microfarad electrolytic capacitor

custom parts:
  Spark Core (v1.0): The Spark Core is a tiny Wi-Fi development board that makes it easy to create internet-connected hardware. The Core is all you need to get started; power it over USB and in minutes you'll be controlling LEDs, switches and motors and collecting data from sensors over the internet! It has 8 digital I/O pins, 8 analog I/O pins, 8 PWM pins; UART (Serial), SPI, I2C, and JTAG peripherals available.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
  Figaro TGS 2602 Gas Sensor: The sensing element is comprised of a metal oxide semiconductor layer formed on the alumina substrate of a sensing chip together with an integrated heater. In the presence of detectable gas, sensor conductivity increases depending on gas concentration in the air. A simple electrical circuit can convert the change in conductivity to an output signal which corresponds to the gas concentration.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
  WSP-2110: This sensor has a very high sensitivity and stability, it can detect the gas whose concentration is up to 1ppm. It’s suitable for detecting formaldehyde, benzene, toluene and other volatile components. This product can be used to detect harmful gas in the home environment. Therefore, it’s a good assistant for you to improve indoor environment quality of life.
  USB Type A Female Breakout Board: USB breakout board for a Type A connector. sparkfun.com
